# Fritzing sketch fritzing (saved by Fritzing 0.9.3b)
perfboards: 1

parts:
  U1 = ESP8266 WiFi Module [part_number=ESP8266]
  IC1 = PICAXE-20M [part_number=r package=THT]
  R1 = Resistor [tolerance=±5% resistance=10k package="0805 [SMD]"]
  U2 = MCP4725 [package=SOT23-6]  # not connected
  JP2 = Header 6 [package=1x06_smd_straight_alt]
  R4 = TRIMPOT [package=3362u-2]
  JP3 = Header 1 [package=1x01_offset]
  JP4 = Header 1 [package=1x01_offset]
  JP5 = Header 1 [package=1x01_offset]
  JP6 = Header 1 [package=1x01_offset]
  JP7 = Header 1 [package=1x01_offset]  # not connected
  JP8 = Header 1 [package=1x01_offset]  # not connected
  JP9 = Header 1 [package=1x01_offset]
  JP10 = Header 1 [package=1x01_offset]

nets:
  N1: U1.RXD, IC1.In_2_/_ADC_2
  N2: U1.TXD, IC1.In_1_/_ADC_1
  N3: R1.Pin_0, JP2.Out
  N4: R1.Pin_1, R4.WIPER, JP4.1, JP5.1
  N5: JP2.Gnd#1, JP10.1
  N6: JP2.VCC, JP9.1
  N7: JP2.Gnd#5, R4.CW, JP3.1, JP6.1

notes:
  Power In (3.3)
  Amplified Audio Out
  To I2C
  PAM Power In
  Pam Audio In

custom parts:
  Header 6: Header 6 Standard 6-pin 0.1 header. Use with straight break away headers (SKU : PRT-00116), right angle break away headers (PRT-00553), swiss pins (PRT-00743), machine pins (PRT-00117), and female headers (PRT-00115). Molex polarized connector foot print use with SKU : PRT-08094 with associated crimp pins and housings. NOTES ON THE VARIANTS LOCK and LOCK_LONGPADS... This footprint was designed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
